# Fritzing sketch RST_BUTTON_Schaltplan (saved by Fritzing 0.9.3b)
breadboards: 1

parts:
  Q1 = PNP-Transistor [package="TO92 [THT]"]
  Adafruit_HUZZAH_ESP8266_Breakout1 = Adafruit HUZZAH ESP8266 Breakout [part_number=2471]
  S1 = Pushbutton [package="[THT]"]
  R1 = Resistor [tolerance=±5% resistance=470 package=THT]
  R2 = Resistor [tolerance=±5% resistance=4.7k package=THT]

nets:
  N1: Q1.E, Adafruit_HUZZAH_ESP8266_Breakout1.#13, S1.Pin_3, S1.Pin_4, R2.Pin_0
  N2: Q1.B, R1.Pin_1
  N3: Q1.C, Adafruit_HUZZAH_ESP8266_Breakout1.RST
  N4: Adafruit_HUZZAH_ESP8266_Breakout1.GND, S1.Pin_1, S1.Pin_2
  N5: Adafruit_HUZZAH_ESP8266_Breakout1.V+, R2.Pin_1
  N6: Adafruit_HUZZAH_ESP8266_Breakout1.#0, R1.Pin_0
